# Fritzing sketch Stimer (saved by Fritzing 0.9.3b)
breadboards: 1

parts:
  FRDM1 = Freescale FRDM KL25Z
  Part1 = Breakout Board for Electret Microphone

nets:
  3.3V: FRDM1.3.3V, Part1.VCC
  GND: FRDM1.GND, Part1.GND
  N1: FRDM1.PTB0, Part1.AUD

notes:
  Tema 9 - Automatski Stimer Gitare
  Grupa 4
  Aćimović Dejan
  Bojadžić Damir

custom parts:
  Freescale FRDM KL25Z: Freescale FRDM razvojni sistem
